// Logisim project Ctl_Conditional.circ as structural Verilog: 1 circuit, main circuit Conditional
module Conditional (
  input  Enable,
  input  [15:0] Instruction,
  input  Z,
  input  C,
  input  N,
  input  V,
  output [10:0] Offset,
  output Verified
);

  wire undriven;

  Multiplexer #(.enable("false")) multiplexer_1 (.in0(undriven), .in1(1'b0), .out(Verified), .sel(Enable));

  // Other names for the same wires on the sheet: EN = Enable
endmodule
